// Logisim project log.circ as structural Verilog
module PC (
  input  [13:0] in_1,
  input  IsJump,
  input  in_3,
  input  in_4
);

  wire [17:0] FEEDBACK, multiplexer_1_out, n18_bit_adder_1_out_3, sign_extension_out_2;

  _14extension sign_extension (.\input (in_1), .out_2(sign_extension_out_2));
  Multiplexer #(.width(18), .enable("false")) multiplexer_1 (
    .in0(18'h1), .in1(sign_extension_out_2), .out(multiplexer_1_out), .sel(IsJump));
  _18_bit_adder u_18_bit_adder_1 (
    .in_1(FEEDBACK), .in_2(multiplexer_1_out), .out_3(n18_bit_adder_1_out_3));  // open: out_4
  Register register_1 (
    .Input_2(n18_bit_adder_1_out_3), .Clr_2(in_3), .in_8(in_4), .out_9(FEEDBACK));  // open: write_2, Input, Clr, in_5, write
  // Probe on FEEDBACK

  // Notes on the sheet:
  //   Coming from control unit and jump to a register or a increamenting with one
endmodule

module ALU (
  input  [17:0] INPUT1,
  input  [17:0] INPUT2,
  input  [1:0] ALU_Control_Input,
  output [17:0] out_4
);

  wire [17:0] and_1_out, n18_bit_adder_1_out_3, nor_1_out, not_1_out;

  _18_bit_adder u_18_bit_adder_1 (.in_1(INPUT1), .in_2(INPUT2), .out_3(n18_bit_adder_1_out_3));  // open: out_4
  assign and_1_out = INPUT1 & INPUT2;  // AND_Gate and_1, 18 bits wide
  assign nor_1_out = ~(INPUT1 | INPUT2);  // NOR_Gate nor_1, 18 bits wide
  assign not_1_out = ~and_1_out;  // NOT_Gate not_1, 18 bits wide
  Multiplexer #(.select(2), .width(18), .enable("false")) multiplexer_1 (
    .in0(n18_bit_adder_1_out_3), .in1(and_1_out), .in2(not_1_out), .in3(nor_1_out), .out(out_4),
    .sel(ALU_Control_Input));

  // Notes on the sheet:
  //   ADD - 00 // AND - 01 // NAND - 10 // NOR - 11 
endmodule

module Register_File (
  input  Clear,
  input  Clock,
  input  [17:0] in_3,
  input  [3:0] in_4
);

  wire decoder_1_out0, decoder_1_out1, decoder_1_out2, decoder_1_out3, decoder_1_out4, decoder_1_out5,
       decoder_1_out6, decoder_1_out7, decoder_1_out8, decoder_1_out9, decoder_1_out10, decoder_1_out11,
       decoder_1_out12, decoder_1_out13, decoder_1_out14, decoder_1_out15, register_1_p8, register_1_p9,
       register_2_p8, register_9_p8, register_9_p9, register_10_p8;

  Decoder #(.select(4), .enable("false")) decoder_1 (
    .out0(decoder_1_out0), .out1(decoder_1_out1), .out2(decoder_1_out2), .out3(decoder_1_out3),
    .out4(decoder_1_out4), .out5(decoder_1_out5), .out6(decoder_1_out6), .out7(decoder_1_out7),
    .out8(decoder_1_out8), .out9(decoder_1_out9), .out10(decoder_1_out10), .out11(decoder_1_out11),
    .out12(decoder_1_out12), .out13(decoder_1_out13), .out14(decoder_1_out14), .out15(decoder_1_out15),
    .sel(in_4));
  // Register register_1: pin names not known; wires that end beside it: in_3, Clear, Clock, decoder_1_out0, decoder_1_out1, in_3, decoder_1_out2, register_1_p8, register_1_p9
  // Register register_2: pin names not known; wires that end beside it: in_3, Clear, Clock, decoder_1_out2, decoder_1_out3, in_3, decoder_1_out4, register_2_p8, register_1_p8
  // Register register_3: pin names not known; wires that end beside it: in_3, Clear, Clock, decoder_1_out4, decoder_1_out5, in_3, decoder_1_out6, register_2_p8
  // Register register_4: pin names not known; wires that end beside it: in_3, Clear, Clock, decoder_1_out6, decoder_1_out7, in_3, decoder_1_out8
  // Register register_5: pin names not known; wires that end beside it: in_3, Clear, Clock, decoder_1_out8, decoder_1_out9, in_3, decoder_1_out10
  // Register register_6: pin names not known; wires that end beside it: in_3, Clear, Clock, decoder_1_out10, decoder_1_out11, in_3, decoder_1_out12
  // Register register_7: pin names not known; wires that end beside it: in_3, Clear, Clock, decoder_1_out12, decoder_1_out13, in_3, decoder_1_out14
  // Register register_8: pin names not known; wires that end beside it: in_3, Clear, Clock, decoder_1_out14, decoder_1_out15
  // Register register_9: pin names not known; wires that end beside it: in_3, Clear, Clock, decoder_1_out1, register_1_p8, in_3, decoder_1_out3, register_9_p8, register_9_p9
  // Register register_10: pin names not known; wires that end beside it: in_3, Clear, Clock, decoder_1_out3, register_2_p8, in_3, decoder_1_out5, register_10_p8, register_9_p8
  // Register register_11: pin names not known; wires that end beside it: in_3, Clear, Clock, decoder_1_out5, in_3, decoder_1_out7, register_10_p8
  // Register register_12: pin names not known; wires that end beside it: in_3, Clear, Clock, decoder_1_out7, in_3, decoder_1_out9
  // Register register_13: pin names not known; wires that end beside it: in_3, Clear, Clock, decoder_1_out9, in_3, decoder_1_out11
  // Register register_14: pin names not known; wires that end beside it: in_3, Clear, Clock, decoder_1_out11, in_3, decoder_1_out13
  // Register register_15: pin names not known; wires that end beside it: in_3, Clear, Clock, decoder_1_out13, in_3, decoder_1_out15
  // Register register_16: pin names not known; wires that end beside it: in_3, Clear, Clock, decoder_1_out15
endmodule

module Register (
  input  [17:0] Input,
  input  [17:0] Input_2,
  input  Clr,
  input  Clr_2,
  input  in_5,
  input  write,
  input  write_2,
  input  in_8,
  output [17:0] out_9
);

  wire undriven;
  wire [1:0] undriven_2;
  wire [17:0] multiplexer_1_out, multiplexer_2_out, multiplexer_3_out;

  Multiplexer #(.width(18), .enable("false")) multiplexer_1 (
    .in0(Input_2), .in1({18{1'b0}}), .out(multiplexer_1_out), .sel(Clr_2));
  Multiplexer #(.width(18), .enable("false")) multiplexer_2 (
    .in0(out_9), .in1(multiplexer_1_out), .out(multiplexer_2_out), .sel(undriven));
  d_flipflop d_flipflop_1 (.D(multiplexer_2_out[0]), .C(in_8), .Q(out_9[0]));
  d_flipflop d_flipflop_2 (.D(multiplexer_2_out[1]), .C(in_8), .Q(out_9[1]));
  d_flipflop d_flipflop_3 (.D(multiplexer_2_out[2]), .C(in_8), .Q(out_9[2]));
  d_flipflop d_flipflop_4 (.D(multiplexer_2_out[3]), .C(in_8), .Q(out_9[3]));
  Multiplexer #(.width(18), .enable("false")) multiplexer_3 (
    .in0(Input), .in1({18{1'b0}}), .out(multiplexer_3_out), .sel(Clr));
  Multiplexer #(.select(2), .width(18), .enable("false")) multiplexer_4 (
    .in0({18{1'b0}}), .in1(out_9), .in2({18{1'b0}}), .in3(multiplexer_3_out), .sel(undriven_2));  // open: out
  d_flipflop d_flipflop_5 (.D(multiplexer_2_out[4]), .C(in_8), .Q(out_9[4]));
  d_flipflop d_flipflop_6 (.D(multiplexer_2_out[5]), .C(in_8), .Q(out_9[5]));
  d_flipflop d_flipflop_7 (.D(multiplexer_2_out[6]), .C(in_8), .Q(out_9[6]));
  d_flipflop d_flipflop_8 (.D(multiplexer_2_out[7]), .C(in_8), .Q(out_9[7]));
  d_flipflop d_flipflop_9 (.D(multiplexer_2_out[8]), .C(in_8), .Q(out_9[8]));
  d_flipflop d_flipflop_10 (.D(multiplexer_2_out[9]), .C(in_8), .Q(out_9[9]));
  d_flipflop d_flipflop_11 (.D(multiplexer_2_out[10]), .C(in_8), .Q(out_9[10]));
  d_flipflop d_flipflop_12 (.D(multiplexer_2_out[11]), .C(in_8), .Q(out_9[11]));
  d_flipflop d_flipflop_13 (.D(multiplexer_2_out[12]), .C(in_8), .Q(out_9[12]));
  d_flipflop d_flipflop_14 (.D(multiplexer_2_out[13]), .C(in_8), .Q(out_9[13]));
  d_flipflop d_flipflop_15 (.D(multiplexer_2_out[14]), .C(in_8), .Q(out_9[14]));
  d_flipflop d_flipflop_16 (.D(multiplexer_2_out[15]), .C(in_8), .Q(out_9[15]));
  d_flipflop d_flipflop_17 (.D(multiplexer_2_out[16]), .C(in_8), .Q(out_9[16]));
  d_flipflop d_flipflop_18 (.D(multiplexer_2_out[17]), .C(in_8), .Q(out_9[17]));

  // Other names for the same wires on the sheet: Back[17:0] = out_9
endmodule

module d_latch (
  input  D,
  input  C,
  output Q
);

  wire and_1_out, and_2_out, nor_1_out, not_1_out;

  not not_1 (not_1_out, D);
  and and_1 (and_1_out, D, C);
  and and_2 (and_2_out, C, not_1_out);
  nor nor_1 (nor_1_out, and_1_out, Q);
  nor nor_2 (Q, nor_1_out, and_2_out);

  // Notes on the sheet:
  //   S
  //   R
  //   S1
  //   R1
endmodule

module d_flipflop (
  input  D,
  input  C,
  output Q
);

  wire d_latch_1_q, not_1_out;

  not not_1 (not_1_out, C);
  d_latch d_latch_1 (.D(D), .C(not_1_out), .Q(d_latch_1_q));
  d_latch d_latch_2 (.D(d_latch_1_q), .C(C), .Q(Q));
endmodule

module _1_bit_adder (
  input  input1,
  input  input2,
  input  carryin,
  output \output ,
  output carryOut
);

  wire and_1_out, and_2_out, and_3_out, and_4_out, and_5_out, and_6_out, and_7_out, not_1_out, not_2_out,
       not_3_out, not_4_out, not_5_out, not_6_out;

  not not_1 (not_1_out, input1);
  not not_2 (not_2_out, input2);
  not not_3 (not_3_out, input1);
  not not_4 (not_4_out, carryin);
  not not_5 (not_5_out, input2);
  not not_6 (not_6_out, carryin);
  and and_1 (and_1_out, input2, carryin);
  and and_2 (and_2_out, input1, carryin);
  and and_3 (and_3_out, input1, input2);
  and and_4 (and_4_out, not_1_out, not_2_out, carryin);
  and and_5 (and_5_out, not_3_out, input2, not_4_out);
  and and_6 (and_6_out, input1, not_5_out, not_6_out);
  and and_7 (and_7_out, input1, input2, carryin);
  or or_1 (carryOut, and_1_out, and_2_out, and_3_out);
  or or_2 (\output , and_4_out, and_5_out, and_6_out, and_7_out);
endmodule

module _18_bit_adder (
  input  [17:0] in_1,
  input  [17:0] in_2,
  output [17:0] out_3,
  output out_4
);

  wire n1_bit_adder_1_carryout, n1_bit_adder_2_carryout, n1_bit_adder_3_carryout, n1_bit_adder_4_carryout,
       n1_bit_adder_5_carryout, n1_bit_adder_6_carryout, n1_bit_adder_7_carryout, n1_bit_adder_8_carryout,
       n1_bit_adder_9_carryout, n1_bit_adder_10_carryout, n1_bit_adder_11_carryout, n1_bit_adder_12_carryout,
       n1_bit_adder_13_carryout, n1_bit_adder_14_carryout, n1_bit_adder_15_carryout,
       n1_bit_adder_16_carryout, n1_bit_adder_17_carryout;

  _1_bit_adder u_1_bit_adder_1 (
    .input1(in_1[0]), .input2(in_2[0]), .carryin(1'b0), .\output (out_3[0]),
    .carryOut(n1_bit_adder_1_carryout));
  _1_bit_adder u_1_bit_adder_2 (
    .input1(in_1[1]), .input2(in_2[1]), .carryin(n1_bit_adder_1_carryout), .\output (out_3[1]),
    .carryOut(n1_bit_adder_2_carryout));
  _1_bit_adder u_1_bit_adder_3 (
    .input1(in_1[2]), .input2(in_2[2]), .carryin(n1_bit_adder_2_carryout), .\output (out_3[2]),
    .carryOut(n1_bit_adder_3_carryout));
  _1_bit_adder u_1_bit_adder_4 (
    .input1(in_1[3]), .input2(in_2[3]), .carryin(n1_bit_adder_3_carryout), .\output (out_3[3]),
    .carryOut(n1_bit_adder_4_carryout));
  _1_bit_adder u_1_bit_adder_5 (
    .input1(in_1[4]), .input2(in_2[4]), .carryin(n1_bit_adder_4_carryout), .\output (out_3[4]),
    .carryOut(n1_bit_adder_5_carryout));
  _1_bit_adder u_1_bit_adder_6 (
    .input1(in_1[5]), .input2(in_2[5]), .carryin(n1_bit_adder_5_carryout), .\output (out_3[5]),
    .carryOut(n1_bit_adder_6_carryout));
  _1_bit_adder u_1_bit_adder_7 (
    .input1(in_1[6]), .input2(in_2[6]), .carryin(n1_bit_adder_6_carryout), .\output (out_3[6]),
    .carryOut(n1_bit_adder_7_carryout));
  _1_bit_adder u_1_bit_adder_8 (
    .input1(in_1[7]), .input2(in_2[7]), .carryin(n1_bit_adder_7_carryout), .\output (out_3[7]),
    .carryOut(n1_bit_adder_8_carryout));
  _1_bit_adder u_1_bit_adder_9 (
    .input1(in_1[8]), .input2(in_2[8]), .carryin(n1_bit_adder_8_carryout), .\output (out_3[8]),
    .carryOut(n1_bit_adder_9_carryout));
  _1_bit_adder u_1_bit_adder_10 (
    .input1(in_1[9]), .input2(in_2[9]), .carryin(n1_bit_adder_9_carryout), .\output (out_3[9]),
    .carryOut(n1_bit_adder_10_carryout));
  _1_bit_adder u_1_bit_adder_11 (
    .input1(in_1[10]), .input2(in_2[10]), .carryin(n1_bit_adder_10_carryout), .\output (out_3[10]),
    .carryOut(n1_bit_adder_11_carryout));
  _1_bit_adder u_1_bit_adder_12 (
    .input1(in_1[11]), .input2(in_2[11]), .carryin(n1_bit_adder_11_carryout), .\output (out_3[11]),
    .carryOut(n1_bit_adder_12_carryout));
  _1_bit_adder u_1_bit_adder_13 (
    .input1(in_1[12]), .input2(in_2[12]), .carryin(n1_bit_adder_12_carryout), .\output (out_3[12]),
    .carryOut(n1_bit_adder_13_carryout));
  _1_bit_adder u_1_bit_adder_14 (
    .input1(in_1[13]), .input2(in_2[13]), .carryin(n1_bit_adder_13_carryout), .\output (out_3[13]),
    .carryOut(n1_bit_adder_14_carryout));
  _1_bit_adder u_1_bit_adder_15 (
    .input1(in_1[14]), .input2(in_2[14]), .carryin(n1_bit_adder_14_carryout), .\output (out_3[14]),
    .carryOut(n1_bit_adder_15_carryout));
  _1_bit_adder u_1_bit_adder_16 (
    .input1(in_1[15]), .input2(in_2[15]), .carryin(n1_bit_adder_15_carryout), .\output (out_3[15]),
    .carryOut(n1_bit_adder_16_carryout));
  _1_bit_adder u_1_bit_adder_17 (
    .input1(in_1[16]), .input2(in_2[16]), .carryin(n1_bit_adder_16_carryout), .\output (out_3[16]),
    .carryOut(n1_bit_adder_17_carryout));
  _1_bit_adder u_1_bit_adder_18 (
    .input1(in_1[17]), .input2(in_2[17]), .carryin(n1_bit_adder_17_carryout), .\output (out_3[17]),
    .carryOut(out_4));
endmodule

module _18extension (
  input  [5:0] \input ,
  output [17:0] \output 
);


  assign \output  = {{13{\input [5]}}, \input [4:0]};
endmodule

module _14extension (
  input  [13:0] \input ,
  output [17:0] out_2
);


  assign out_2 = {{5{\input [13]}}, \input [12:0]};
endmodule
