// Logisim project log.circ as structural Verilog: 14 circuits, main circuit CPU
module CPU (
);

  PC pc_1 ();  // open: in_1, in_2, in_3, IsJump, out_7, in_5, in_6
  ROM rom_1 ();  // open: addr, data, sel
  Register_File register_file_1 ();  // open: in_3, Write_Bit, Output, Clock, Clear, Enable, Read_Bit
  ALU alu_1 ();  // open: INPUT1, INPUT2, ALU_Control_Input, out_4
  RAM ram_1 ();  // open: addr, data, sel, clk, ld, clr
endmodule

module Control_Unit (
  input  in_1
);

  wire [3:0] DST, Opcode, SRC1;
  wire [5:0] SRC2_IMM;
  wire [9:0] counter_1_q;
  wire [19:18] rom_1_data;

  Counter #(.width(10), .max('h3ff)) counter_1 (.Q(counter_1_q), .clk(in_1));  // open: load, D, count, carry, clr
  ROM #(.addrWidth(10), .dataWidth(20)) rom_1 (
    .addr(counter_1_q), .data({rom_1_data, Opcode, DST, SRC1, SRC2_IMM}));  // open: sel
  Multiplexer #(.select(4), .enable("false")) multiplexer_1 (.sel(Opcode));  // open: in0, in1, in2, in3, in4, in5, in6, in7, in8, in9, in10, in11, in12, in13, in14, in15, out

  // Notes on the sheet:
  //   contents of rom_1 (hex, n*v repeats v):
  //   1402 4c4c 8483 cd37 115c9 16ccf 1a1ff 1e5a3 22f58 24002 2a140 2d51f 3282d 3456a 3b465
endmodule

module PC (
  input  in_1,
  input  [13:0] in_2,
  input  in_3,
  input  IsJump,
  input  in_5,
  input  in_6,
  output [17:0] out_7
);

  wire [17:0] multiplexer_1_out, n18_bit_adder_1_out_3, sign_extension_out_2;

  _14_18extender sign_extension (.\input (in_2), .out_2(sign_extension_out_2));
  Multiplexer #(.width(18), .enable("false")) multiplexer_1 (
    .in0(18'h1), .in1(sign_extension_out_2), .out(multiplexer_1_out), .sel(IsJump));
  _18_bit_adder u_18_bit_adder_1 (
    .in_1(out_7), .in_2(multiplexer_1_out), .out_3(n18_bit_adder_1_out_3));  // open: out_4
  Register register_1 (
    .in_5(in_6), .out_6(out_7), .Input(n18_bit_adder_1_out_3), .Clr(in_1), .write(in_5), .in_4(in_3));
  // Probe on out_7

  // Other names for the same wires on the sheet: FEEDBACK[17:0] = out_7

  // Notes on the sheet:
  //   Coming from control unit and jump to a register or a increamenting with one
endmodule

module Register_File (
  input  Clock,
  input  Clear,
  input  [17:0] in_3,
  input  [3:0] Read_Bit,
  input  [3:0] Write_Bit,
  input  Enable,
  output [17:0] Output
);

  wire decoder_1_out0, decoder_1_out1, decoder_1_out2, decoder_1_out3, decoder_1_out4, decoder_1_out5,
       decoder_1_out6, decoder_1_out7, decoder_1_out8, decoder_1_out9, decoder_1_out10, decoder_1_out11,
       decoder_1_out12, decoder_1_out13, decoder_1_out14, decoder_1_out15;
  wire [17:0] register_1_out_6, register_2_out_6, register_3_out_6, register_4_out_6, register_5_out_6,
       register_6_out_6, register_7_out_6, register_8_out_6, register_9_out_6, register_10_out_6,
       register_11_out_6, register_12_out_6, register_13_out_6, register_14_out_6, register_15_out_6,
       register_16_out_6;

  Decoder #(.select(4), .enable("false")) decoder_1 (
    .out0(decoder_1_out0), .out1(decoder_1_out1), .out2(decoder_1_out2), .out3(decoder_1_out3),
    .out4(decoder_1_out4), .out5(decoder_1_out5), .out6(decoder_1_out6), .out7(decoder_1_out7),
    .out8(decoder_1_out8), .out9(decoder_1_out9), .out10(decoder_1_out10), .out11(decoder_1_out11),
    .out12(decoder_1_out12), .out13(decoder_1_out13), .out14(decoder_1_out14), .out15(decoder_1_out15),
    .sel(Write_Bit));
  Register register_1 (
    .in_5(Clock), .out_6(register_1_out_6), .Input(in_3), .Clr(Clear), .write(decoder_1_out0), .in_4(Enable));
  Register register_2 (
    .in_5(Clock), .out_6(register_2_out_6), .Input(in_3), .Clr(Clear), .write(decoder_1_out2), .in_4(Enable));
  Register register_3 (
    .in_5(Clock), .out_6(register_3_out_6), .Input(in_3), .Clr(Clear), .write(decoder_1_out4), .in_4(Enable));
  Register register_4 (
    .in_5(Clock), .out_6(register_4_out_6), .Input(in_3), .Clr(Clear), .write(decoder_1_out6), .in_4(Enable));
  Register register_5 (
    .in_5(Clock), .out_6(register_5_out_6), .Input(in_3), .Clr(Clear), .write(decoder_1_out8), .in_4(Enable));
  Register register_6 (
    .in_5(Clock), .out_6(register_6_out_6), .Input(in_3), .Clr(Clear), .write(decoder_1_out10), .in_4(Enable));
  Register register_7 (
    .in_5(Clock), .out_6(register_7_out_6), .Input(in_3), .Clr(Clear), .write(decoder_1_out12), .in_4(Enable));
  Register register_8 (
    .in_5(Clock), .out_6(register_8_out_6), .Input(in_3), .Clr(Clear), .write(decoder_1_out14), .in_4(Enable));
  Register register_9 (
    .in_5(Clock), .out_6(register_9_out_6), .Input(in_3), .Clr(Clear), .write(decoder_1_out1), .in_4(Enable));
  Register register_10 (
    .in_5(Clock), .out_6(register_10_out_6), .Input(in_3), .Clr(Clear), .write(decoder_1_out3), .in_4(Enable));
  Register register_11 (
    .in_5(Clock), .out_6(register_11_out_6), .Input(in_3), .Clr(Clear), .write(decoder_1_out5), .in_4(Enable));
  Register register_12 (
    .in_5(Clock), .out_6(register_12_out_6), .Input(in_3), .Clr(Clear), .write(decoder_1_out7), .in_4(Enable));
  Register register_13 (
    .in_5(Clock), .out_6(register_13_out_6), .Input(in_3), .Clr(Clear), .write(decoder_1_out9), .in_4(Enable));
  Register register_14 (
    .in_5(Clock), .out_6(register_14_out_6), .Input(in_3), .Clr(Clear), .write(decoder_1_out11), .in_4(Enable));
  Register register_15 (
    .in_5(Clock), .out_6(register_15_out_6), .Input(in_3), .Clr(Clear), .write(decoder_1_out13), .in_4(Enable));
  Register register_16 (
    .in_5(Clock), .out_6(register_16_out_6), .Input(in_3), .Clr(Clear), .write(decoder_1_out15), .in_4(Enable));
  Multiplexer #(.select(4), .width(18), .enable("false")) multiplexer_1 (
    .in0(register_1_out_6), .in1(register_9_out_6), .in2(register_2_out_6), .in3(register_10_out_6),
    .in4(register_3_out_6), .in5(register_11_out_6), .in6(register_4_out_6), .in7(register_12_out_6),
    .in8(register_5_out_6), .in9(register_13_out_6), .in10(register_6_out_6), .in11(register_14_out_6),
    .in12(register_7_out_6), .in13(register_15_out_6), .in14(register_8_out_6), .in15(register_16_out_6),
    .out(Output), .sel(Read_Bit));
endmodule

module ALU (
  input  [17:0] INPUT1,
  input  [17:0] INPUT2,
  input  [1:0] ALU_Control_Input,
  output [17:0] out_4
);

  wire [17:0] and_1_out, n18_bit_adder_1_out_3, nor_1_out, not_1_out;

  _18_bit_adder u_18_bit_adder_1 (.in_1(INPUT1), .in_2(INPUT2), .out_3(n18_bit_adder_1_out_3));  // open: out_4
  assign and_1_out = INPUT1 & INPUT2;  // AND_Gate and_1, 18 bits wide
  assign nor_1_out = ~(INPUT1 | INPUT2);  // NOR_Gate nor_1, 18 bits wide
  assign not_1_out = ~and_1_out;  // NOT_Gate not_1, 18 bits wide
  Multiplexer #(.select(2), .width(18), .enable("false")) multiplexer_1 (
    .in0(n18_bit_adder_1_out_3), .in1(and_1_out), .in2(not_1_out), .in3(nor_1_out), .out(out_4),
    .sel(ALU_Control_Input));

  // Notes on the sheet:
  //   ADD - 00 // AND - 01 // NAND - 10 // NOR - 11 
endmodule

module Register (
  input  [17:0] Input,
  input  Clr,
  input  write,
  input  in_4,
  input  in_5,
  output [17:0] out_6
);

  wire zero;
  wire [0:0] decoder_1_out1;
  wire [17:0] d_flipflop_1_q, multiplexer_1_out, multiplexer_2_out;

  Multiplexer #(.width(18), .enable("false")) multiplexer_1 (
    .in0(Input), .in1({18{1'b0}}), .out(multiplexer_1_out), .sel(Clr));
  Multiplexer #(.select(2), .width(18), .enable("false")) multiplexer_2 (
    .in0({18{1'b0}}), .in1(out_6), .in2({18{1'b0}}), .in3(multiplexer_1_out), .out(multiplexer_2_out),
    .sel({write, decoder_1_out1[0]}));
  d_flipflop d_flipflop_1 (.D(multiplexer_2_out[0]), .C(in_5), .Q(d_flipflop_1_q[0]));
  d_flipflop d_flipflop_2 (.D(multiplexer_2_out[1]), .C(in_5), .Q(d_flipflop_1_q[1]));
  d_flipflop d_flipflop_3 (.D(multiplexer_2_out[2]), .C(in_5), .Q(d_flipflop_1_q[2]));
  Decoder #(.disabled(0), .enable("false")) decoder_1 (.out0(zero), .out1(decoder_1_out1[0]), .sel(in_4));
  d_flipflop d_flipflop_4 (.D(multiplexer_2_out[3]), .C(in_5), .Q(d_flipflop_1_q[3]));
  d_flipflop d_flipflop_5 (.D(multiplexer_2_out[4]), .C(in_5), .Q(d_flipflop_1_q[4]));
  d_flipflop d_flipflop_6 (.D(multiplexer_2_out[5]), .C(in_5), .Q(d_flipflop_1_q[5]));
  Multiplexer #(.width(18), .enable("false")) multiplexer_3 (
    .in0(d_flipflop_1_q), .in1({18{1'b0}}), .out(out_6), .sel(zero));
  d_flipflop d_flipflop_7 (.D(multiplexer_2_out[6]), .C(in_5), .Q(d_flipflop_1_q[6]));
  d_flipflop d_flipflop_8 (.D(multiplexer_2_out[7]), .C(in_5), .Q(d_flipflop_1_q[7]));
  d_flipflop d_flipflop_9 (.D(multiplexer_2_out[8]), .C(in_5), .Q(d_flipflop_1_q[8]));
  d_flipflop d_flipflop_10 (.D(multiplexer_2_out[9]), .C(in_5), .Q(d_flipflop_1_q[9]));
  d_flipflop d_flipflop_11 (.D(multiplexer_2_out[10]), .C(in_5), .Q(d_flipflop_1_q[10]));
  d_flipflop d_flipflop_12 (.D(multiplexer_2_out[11]), .C(in_5), .Q(d_flipflop_1_q[11]));
  d_flipflop d_flipflop_13 (.D(multiplexer_2_out[12]), .C(in_5), .Q(d_flipflop_1_q[12]));
  d_flipflop d_flipflop_14 (.D(multiplexer_2_out[13]), .C(in_5), .Q(d_flipflop_1_q[13]));
  d_flipflop d_flipflop_15 (.D(multiplexer_2_out[14]), .C(in_5), .Q(d_flipflop_1_q[14]));
  d_flipflop d_flipflop_16 (.D(multiplexer_2_out[15]), .C(in_5), .Q(d_flipflop_1_q[15]));
  d_flipflop d_flipflop_17 (.D(multiplexer_2_out[16]), .C(in_5), .Q(d_flipflop_1_q[16]));
  d_flipflop d_flipflop_18 (.D(multiplexer_2_out[17]), .C(in_5), .Q(d_flipflop_1_q[17]));

  // Other names for the same wires on the sheet: Back[17:0] = out_6
endmodule

module d_latch (
  input  D,
  input  C,
  output Q
);

  wire and_1_out, and_2_out, nor_1_out, not_1_out;

  not not_1 (not_1_out, D);
  and and_1 (and_1_out, D, C);
  and and_2 (and_2_out, C, not_1_out);
  nor nor_1 (nor_1_out, and_1_out, Q);
  nor nor_2 (Q, nor_1_out, and_2_out);

  // Notes on the sheet:
  //   S
  //   R
  //   S1
  //   R1
endmodule

module d_flipflop (
  input  D,
  input  C,
  output Q
);

  wire d_latch_1_q, not_1_out;

  not not_1 (not_1_out, C);
  d_latch d_latch_1 (.D(D), .C(not_1_out), .Q(d_latch_1_q));
  d_latch d_latch_2 (.D(d_latch_1_q), .C(C), .Q(Q));
endmodule

module _1_bit_adder (
  input  input1,
  input  input2,
  input  carryin,
  output \output ,
  output carryOut
);

  wire and_1_out, and_2_out, and_3_out;

  and and_1 (and_1_out, input1, input2);
  and and_2 (and_2_out, carryin, input2);
  and and_3 (and_3_out, input1, carryin);
  xor xor_1 (\output , input1, input2, carryin);
  or or_1 (carryOut, and_1_out, and_2_out, and_3_out);
endmodule

module _18_bit_adder (
  input  [17:0] in_1,
  input  [17:0] in_2,
  output [17:0] out_3,
  output out_4
);

  wire n1_bit_adder_1_carryout, n1_bit_adder_2_carryout, n1_bit_adder_3_carryout, n1_bit_adder_4_carryout,
       n1_bit_adder_5_carryout, n1_bit_adder_6_carryout, n1_bit_adder_7_carryout, n1_bit_adder_8_carryout,
       n1_bit_adder_9_carryout, n1_bit_adder_10_carryout, n1_bit_adder_11_carryout, n1_bit_adder_12_carryout,
       n1_bit_adder_13_carryout, n1_bit_adder_14_carryout, n1_bit_adder_15_carryout,
       n1_bit_adder_16_carryout, n1_bit_adder_17_carryout;

  _1_bit_adder u_1_bit_adder_1 (
    .input1(in_1[0]), .input2(in_2[0]), .carryin(1'b0), .\output (out_3[0]),
    .carryOut(n1_bit_adder_1_carryout));
  _1_bit_adder u_1_bit_adder_2 (
    .input1(in_1[1]), .input2(in_2[1]), .carryin(n1_bit_adder_1_carryout), .\output (out_3[1]),
    .carryOut(n1_bit_adder_2_carryout));
  _1_bit_adder u_1_bit_adder_3 (
    .input1(in_1[2]), .input2(in_2[2]), .carryin(n1_bit_adder_2_carryout), .\output (out_3[2]),
    .carryOut(n1_bit_adder_3_carryout));
  _1_bit_adder u_1_bit_adder_4 (
    .input1(in_1[3]), .input2(in_2[3]), .carryin(n1_bit_adder_3_carryout), .\output (out_3[3]),
    .carryOut(n1_bit_adder_4_carryout));
  _1_bit_adder u_1_bit_adder_5 (
    .input1(in_1[4]), .input2(in_2[4]), .carryin(n1_bit_adder_4_carryout), .\output (out_3[4]),
    .carryOut(n1_bit_adder_5_carryout));
  _1_bit_adder u_1_bit_adder_6 (
    .input1(in_1[5]), .input2(in_2[5]), .carryin(n1_bit_adder_5_carryout), .\output (out_3[5]),
    .carryOut(n1_bit_adder_6_carryout));
  _1_bit_adder u_1_bit_adder_7 (
    .input1(in_1[6]), .input2(in_2[6]), .carryin(n1_bit_adder_6_carryout), .\output (out_3[6]),
    .carryOut(n1_bit_adder_7_carryout));
  _1_bit_adder u_1_bit_adder_8 (
    .input1(in_1[7]), .input2(in_2[7]), .carryin(n1_bit_adder_7_carryout), .\output (out_3[7]),
    .carryOut(n1_bit_adder_8_carryout));
  _1_bit_adder u_1_bit_adder_9 (
    .input1(in_1[8]), .input2(in_2[8]), .carryin(n1_bit_adder_8_carryout), .\output (out_3[8]),
    .carryOut(n1_bit_adder_9_carryout));
  _1_bit_adder u_1_bit_adder_10 (
    .input1(in_1[9]), .input2(in_2[9]), .carryin(n1_bit_adder_9_carryout), .\output (out_3[9]),
    .carryOut(n1_bit_adder_10_carryout));
  _1_bit_adder u_1_bit_adder_11 (
    .input1(in_1[10]), .input2(in_2[10]), .carryin(n1_bit_adder_10_carryout), .\output (out_3[10]),
    .carryOut(n1_bit_adder_11_carryout));
  _1_bit_adder u_1_bit_adder_12 (
    .input1(in_1[11]), .input2(in_2[11]), .carryin(n1_bit_adder_11_carryout), .\output (out_3[11]),
    .carryOut(n1_bit_adder_12_carryout));
  _1_bit_adder u_1_bit_adder_13 (
    .input1(in_1[12]), .input2(in_2[12]), .carryin(n1_bit_adder_12_carryout), .\output (out_3[12]),
    .carryOut(n1_bit_adder_13_carryout));
  _1_bit_adder u_1_bit_adder_14 (
    .input1(in_1[13]), .input2(in_2[13]), .carryin(n1_bit_adder_13_carryout), .\output (out_3[13]),
    .carryOut(n1_bit_adder_14_carryout));
  _1_bit_adder u_1_bit_adder_15 (
    .input1(in_1[14]), .input2(in_2[14]), .carryin(n1_bit_adder_14_carryout), .\output (out_3[14]),
    .carryOut(n1_bit_adder_15_carryout));
  _1_bit_adder u_1_bit_adder_16 (
    .input1(in_1[15]), .input2(in_2[15]), .carryin(n1_bit_adder_15_carryout), .\output (out_3[15]),
    .carryOut(n1_bit_adder_16_carryout));
  _1_bit_adder u_1_bit_adder_17 (
    .input1(in_1[16]), .input2(in_2[16]), .carryin(n1_bit_adder_16_carryout), .\output (out_3[16]),
    .carryOut(n1_bit_adder_17_carryout));
  _1_bit_adder u_1_bit_adder_18 (
    .input1(in_1[17]), .input2(in_2[17]), .carryin(n1_bit_adder_17_carryout), .\output (out_3[17]),
    .carryOut(out_4));
endmodule

module _6_18extender (
  input  [5:0] \input ,
  output [17:0] \output 
);


  assign \output  = {{13{\input [5]}}, \input [4:0]};
endmodule

module _14_18extender (
  input  [13:0] \input ,
  output [17:0] out_2
);


  assign out_2 = {{5{\input [13]}}, \input [12:0]};
endmodule

module _18_bit_comperator (
  input  [17:0] in_1,
  input  [17:0] in_2,
  output out_3,
  output out_4,
  output out_5
);

  wire not_1_out, not_2_out;
  wire [16:0] n18_bit_adder_1_out_3;
  wire [17:0] n18_bit_revers_1_out_2;

  _18_bit_revers u_18_bit_revers_1 (.in_1(in_1), .out_2(n18_bit_revers_1_out_2));
  _18_bit_adder u_18_bit_adder_1 (
    .in_1(n18_bit_revers_1_out_2), .in_2(in_2), .out_3({out_3, n18_bit_adder_1_out_3}));  // open: out_4
  not not_1 (not_1_out, out_3);
  not not_2 (not_2_out, out_4);
  and and_1 (out_5, not_1_out, not_2_out);
  // Probe on {out_3, n18_bit_adder_1_out_3}
  nor nor_1 (out_4, out_3, n18_bit_adder_1_out_3[16], n18_bit_adder_1_out_3[15], n18_bit_adder_1_out_3[14], n18_bit_adder_1_out_3[13], n18_bit_adder_1_out_3[12], n18_bit_adder_1_out_3[11], n18_bit_adder_1_out_3[10], n18_bit_adder_1_out_3[9], n18_bit_adder_1_out_3[8], n18_bit_adder_1_out_3[7], n18_bit_adder_1_out_3[6], n18_bit_adder_1_out_3[5], n18_bit_adder_1_out_3[4], n18_bit_adder_1_out_3[3], n18_bit_adder_1_out_3[2], n18_bit_adder_1_out_3[1], n18_bit_adder_1_out_3[0]);
endmodule

// Reverser
module _18_bit_revers (
  input  [17:0] in_1,
  output [17:0] out_2
);

  wire [17:0] not_1_out;

  assign not_1_out = ~in_1;  // NOT_Gate not_1, 18 bits wide
  _18_bit_adder u_18_bit_adder_1 (.in_1(18'h1), .in_2(not_1_out), .out_3(out_2));  // open: out_4
endmodule
