// Logisim project log.circ as structural Verilog: 14 circuits, main circuit CPU
module CPU (
);

  wire abv, ba, blw, clock_1_out, control_unit_1_isimm, control_unit_1_isjump, control_unit_1_mem_to_reg,
       control_unit_1_out_11, control_unit_1_out_13, control_unit_1_write_mem_enable,
       control_unit_1_write_reg_enable, not_1_out;
  wire [1:0] control_unit_1_alucontrol;
  wire [3:0] control_unit_1_dst, control_unit_1_src1, control_unit_1_src2;
  wire [5:0] control_unit_1_imm;
  wire [9:0] control_unit_1_mem_address;
  wire [13:0] control_unit_1_jump_address;
  wire [17:0] controlled_buffer_2_out, multiplexer_1_out, n6_18extender_1_output, pc_1_out_6, ram_1_data,
       register_file_1_output, register_file_1_output_1;
  wire [19:0] ins;

  Clock clock_1 (.out(clock_1_out));
  PC pc_1 (
    .in_2(control_unit_1_jump_address), .IsJump(control_unit_1_isjump), .out_6(pc_1_out_6),
    .in_4(control_unit_1_out_13), .in_5(clock_1_out), .in_1(control_unit_1_out_11));
  Control_Unit control_unit_1 (
    .in_1(ins), .AluControl(control_unit_1_alucontrol), .out_11(control_unit_1_out_11),
    .out_13(control_unit_1_out_13), .SRC2(control_unit_1_src2), .IMM(control_unit_1_imm),
    .SRC1(control_unit_1_src1), .in_2(clock_1_out), .DST(control_unit_1_dst),
    .Write_Reg_Enable(control_unit_1_write_reg_enable), .IsIMM(control_unit_1_isimm),
    .Write_Mem_Enable(control_unit_1_write_mem_enable), .Mem_Address(control_unit_1_mem_address),
    .mem_to_reg(control_unit_1_mem_to_reg), .in_3(abv), .in_4(ba), .in_5(blw),
    .isJump(control_unit_1_isjump), .Jump_Address(control_unit_1_jump_address));
  ROM #(.addrWidth(18), .dataWidth(20)) rom_1 (.addr(pc_1_out_6), .data(ins));  // open: sel
  RAM #(.addrWidth(10), .dataWidth(18)) ram_1 (
    .addr(control_unit_1_mem_address), .data(ram_1_data), .clk(clock_1_out), .ld(not_1_out));  // open: sel, clr
  not not_1 (not_1_out, control_unit_1_write_mem_enable);
  Multiplexer #(.width(18), .enable("false")) multiplexer_1 (
    .in0(register_file_1_output), .in1(n6_18extender_1_output), .out(multiplexer_1_out),
    .sel(control_unit_1_isimm));
  _6_18extender u_6_18extender_1 (.\input (control_unit_1_imm), .\output (n6_18extender_1_output));
  Register_File register_file_1 (
    .in_3(controlled_buffer_2_out), .Write_Bit(control_unit_1_dst), .Clock(clock_1_out),
    .Clear(control_unit_1_out_11), .Read_1_Bit(control_unit_1_src1), .Output_1(register_file_1_output_1),
    .Read_2_Bit(control_unit_1_src2), .Output(register_file_1_output), .in_7(control_unit_1_write_reg_enable));
  assign ram_1_data = control_unit_1_write_mem_enable ? register_file_1_output_1 : 18'bz;  // Controlled_Buffer controlled_buffer_1
  assign controlled_buffer_2_out = control_unit_1_mem_to_reg ? ram_1_data : 18'bz;  // Controlled_Buffer controlled_buffer_2
  ALU alu_1 (
    .INPUT1(register_file_1_output_1), .INPUT2(multiplexer_1_out),
    .ALU_Control_Input(control_unit_1_alucontrol), .out_4(controlled_buffer_2_out));
  _18_bit_comperator u_18_bit_comperator_1 (
    .in_1(register_file_1_output_1), .in_2(register_file_1_output), .out_3(blw), .out_5(abv), .out_4(ba));

  // Notes on the sheet:
  //   contents of rom_1 (hex, n*v repeats v):
  //   24001 28008
endmodule

module Control_Unit (
  input  [19:0] in_1,
  input  in_2,
  input  in_3,
  input  in_4,
  input  in_5,
  output [1:0] AluControl,
  output [5:0] IMM,
  output [3:0] SRC2,
  output IsIMM,
  output [13:0] Jump_Address,
  output out_11,
  output [3:0] SRC1,
  output out_13,
  output [3:0] DST,
  output Write_Mem_Enable,
  output isJump,
  output Write_Reg_Enable,
  output [9:0] Mem_Address,
  output mem_to_reg
);

  wire ADD, ADDI, AND, and_1_out, and_2_out, and_3_out, and_4_out, and_5_out, and_6_out, and_7_out, ANDI,
       CMP, d_flipflop_1_q, d_flipflop_2_q, d_flipflop_3_q, decoder_2_out15, fetch, fetch_operands, fetch_t,
       JA, JAE, JB, JBE, JE, Jump, LD, NAND, NOR, not_1_out, or_1_out, or_3_out, ST, store;
  wire [1:0] counter_1_q, NextState;
  wire [5:4] demultiplexer_1_out0;

  // Probe on NextState
  not not_1 (not_1_out, or_1_out);
  or or_1 (or_1_out, store, out_11);
  Counter #(.width(2), .max('h3), .trigger("falling")) counter_1 (
    .load(or_1_out), .D(NextState), .count(not_1_out), .Q(counter_1_q), .clk(in_2));  // open: carry, clr
  Decoder #(.select(2), .enable("false")) decoder_1 (
    .out0(out_11), .out1(fetch), .out2(fetch_operands), .out3(store), .sel(counter_1_q));
  Multiplexer #(.width(2), .enable("false")) multiplexer_1 (.in0(2'b10), .in1(2'b01), .out(NextState), .sel(store));
  d_flipflop d_flipflop_1 (.D(in_3), .C(fetch_t), .Q(d_flipflop_1_q));
  d_flipflop d_flipflop_2 (.D(in_4), .C(fetch_t), .Q(d_flipflop_2_q));
  d_flipflop d_flipflop_3 (.D(in_5), .C(fetch_t), .Q(d_flipflop_3_q));
  or or_2 (out_13, out_11, fetch);
  and and_1 (and_1_out, d_flipflop_3_q, JB);
  and and_2 (and_2_out, d_flipflop_3_q, JBE);
  and and_3 (and_3_out, JA, d_flipflop_1_q);
  and and_4 (and_4_out, JAE, d_flipflop_1_q);
  and and_5 (and_5_out, d_flipflop_2_q, JE);
  and and_6 (and_6_out, d_flipflop_2_q, JAE);
  and and_7 (and_7_out, d_flipflop_2_q, JBE);
  Decoder #(.select(4), .enable("false")) decoder_2 (
    .out0(ADD), .out1(ADDI), .out2(AND), .out3(ANDI), .out4(NAND), .out5(NOR), .out6(LD), .out7(ST),
    .out8(Jump), .out9(CMP), .out10(JE), .out11(JA), .out12(JB), .out13(JAE), .out14(JBE),
    .out15(decoder_2_out15), .sel(in_1[17:14]));
  or or_3 (or_3_out, and_3_out, and_4_out, and_5_out, and_6_out, and_7_out, and_1_out, and_2_out);
  or or_4 (isJump, or_3_out, Jump);
  assign IsIMM = ADD ? 1'b0 : 1'bz;  // Controlled_Buffer controlled_buffer_1
  assign AluControl = ADD ? 2'b00 : 2'bz;  // Controlled_Buffer controlled_buffer_2
  assign IsIMM = ADDI ? 1'b1 : 1'bz;  // Controlled_Buffer controlled_buffer_3
  assign AluControl = ADDI ? 2'b00 : 2'bz;  // Controlled_Buffer controlled_buffer_4
  assign IsIMM = AND ? 1'b0 : 1'bz;  // Controlled_Buffer controlled_buffer_5
  assign AluControl = AND ? 2'b01 : 2'bz;  // Controlled_Buffer controlled_buffer_6
  assign IsIMM = ANDI ? 1'b1 : 1'bz;  // Controlled_Buffer controlled_buffer_7
  assign AluControl = ANDI ? 2'b01 : 2'bz;  // Controlled_Buffer controlled_buffer_8
  assign IsIMM = NAND ? 1'b0 : 1'bz;  // Controlled_Buffer controlled_buffer_9
  assign AluControl = NAND ? 2'b10 : 2'bz;  // Controlled_Buffer controlled_buffer_10
  assign IsIMM = NOR ? 1'b0 : 1'bz;  // Controlled_Buffer controlled_buffer_11
  assign AluControl = NOR ? 2'b11 : 2'bz;  // Controlled_Buffer controlled_buffer_12
  and and_8 (Write_Reg_Enable, store, ~ST, ~CMP, ~JE, ~JA, ~JAE, ~JB, ~JBE, ~Jump);  // AND_Gate
  assign IsIMM = CMP ? CMP : 1'bz;  // Controlled_Buffer controlled_buffer_13
  Demultiplexer #(.width(6), .enable("false")) demultiplexer_1 (
    .out0({demultiplexer_1_out0, SRC2}), .out1(IMM), .in(in_1[5:0]), .sel(IsIMM));
  and and_9 (Write_Mem_Enable, store, ST);
  and and_10 (mem_to_reg, store, LD);

  assign DST = in_1[13:10];
  assign Jump_Address = in_1[13:0];
  assign Mem_Address = in_1[9:0];
  assign SRC1 = in_1[9:6];

  // Other names for the same wires on the sheet: ADDRESS[9:0] = in_1[9:0]; Other[13:0] = in_1[13:0];
  //   SRC2_IMM[5:0] = in_1[5:0]; DST_SRC[3:0] = in_1[13:10]; DST_t[3:0] = in_1[13:10]; init_pc = out_11;
  //   Opcode[3:0] = in_1[17:14]

  // Notes on the sheet:
  //   ADD AND NOR ETC
  //   LD STR 
endmodule

module PC (
  input  in_1,
  input  [13:0] in_2,
  input  IsJump,
  input  in_4,
  input  in_5,
  output [17:0] out_6
);

  wire [17:0] multiplexer_1_out, n18_bit_adder_1_out_3, sign_extension_out_2;

  _14_18extender sign_extension (.\input (in_2), .out_2(sign_extension_out_2));
  Multiplexer #(.width(18), .enable("false")) multiplexer_1 (
    .in0(18'h1), .in1(sign_extension_out_2), .out(multiplexer_1_out), .sel(IsJump));
  _18_bit_adder u_18_bit_adder_1 (
    .in_1(out_6), .in_2(multiplexer_1_out), .out_3(n18_bit_adder_1_out_3));  // open: out_4
  Register register_1 (.in_4(in_5), .out_5(out_6), .Input(n18_bit_adder_1_out_3), .Clr(in_1), .in_3(in_4));
  // Probe on out_6

  // Other names for the same wires on the sheet: FEEDBACK[17:0] = out_6

  // Notes on the sheet:
  //   Coming from control unit and jump to a register or a increamenting with one
endmodule

module Register_File (
  input  Clock,
  input  Clear,
  input  [17:0] in_3,
  input  [3:0] Read_1_Bit,
  input  [3:0] Write_Bit,
  input  [3:0] Read_2_Bit,
  input  in_7,
  output [17:0] Output_1,
  output [17:0] Output
);

  wire and_1_out, and_2_out, and_3_out, and_4_out, and_5_out, and_6_out, and_7_out, and_8_out, and_9_out,
       and_10_out, and_11_out, and_12_out, and_13_out, and_14_out, and_15_out, and_16_out, decoder_1_out0,
       decoder_1_out1, decoder_1_out2, decoder_1_out3, decoder_1_out4, decoder_1_out5, decoder_1_out6,
       decoder_1_out7, decoder_1_out8, decoder_1_out9, decoder_1_out10, decoder_1_out11, decoder_1_out12,
       decoder_1_out13, decoder_1_out14, decoder_1_out15;
  wire [17:0] register_1_out_5, register_2_out_5, register_3_out_5, register_4_out_5, register_5_out_5,
       register_6_out_5, register_7_out_5, register_8_out_5, register_9_out_5, register_10_out_5,
       register_11_out_5, register_12_out_5, register_13_out_5, register_14_out_5, register_15_out_5,
       register_16_out_5;

  Decoder #(.select(4), .enable("false")) decoder_1 (
    .out0(decoder_1_out0), .out1(decoder_1_out1), .out2(decoder_1_out2), .out3(decoder_1_out3),
    .out4(decoder_1_out4), .out5(decoder_1_out5), .out6(decoder_1_out6), .out7(decoder_1_out7),
    .out8(decoder_1_out8), .out9(decoder_1_out9), .out10(decoder_1_out10), .out11(decoder_1_out11),
    .out12(decoder_1_out12), .out13(decoder_1_out13), .out14(decoder_1_out14), .out15(decoder_1_out15),
    .sel(Write_Bit));
  and and_1 (and_1_out, decoder_1_out0, in_7);
  and and_2 (and_2_out, decoder_1_out1, in_7);
  and and_3 (and_3_out, decoder_1_out2, in_7);
  and and_4 (and_4_out, decoder_1_out3, in_7);
  and and_5 (and_5_out, decoder_1_out4, in_7);
  and and_6 (and_6_out, decoder_1_out5, in_7);
  and and_7 (and_7_out, decoder_1_out6, in_7);
  and and_8 (and_8_out, decoder_1_out7, in_7);
  and and_9 (and_9_out, decoder_1_out8, in_7);
  and and_10 (and_10_out, decoder_1_out9, in_7);
  and and_11 (and_11_out, decoder_1_out10, in_7);
  and and_12 (and_12_out, decoder_1_out11, in_7);
  and and_13 (and_13_out, decoder_1_out12, in_7);
  and and_14 (and_14_out, decoder_1_out13, in_7);
  and and_15 (and_15_out, decoder_1_out14, in_7);
  and and_16 (and_16_out, decoder_1_out15, in_7);
  Register register_1 (.in_4(Clock), .out_5(register_1_out_5), .Input(in_3), .Clr(Clear), .in_3(and_1_out));
  Register register_2 (.in_4(Clock), .out_5(register_2_out_5), .Input(in_3), .Clr(Clear), .in_3(and_3_out));
  Register register_3 (.in_4(Clock), .out_5(register_3_out_5), .Input(in_3), .Clr(Clear), .in_3(and_5_out));
  Register register_4 (.in_4(Clock), .out_5(register_4_out_5), .Input(in_3), .Clr(Clear), .in_3(and_7_out));
  Register register_5 (.in_4(Clock), .out_5(register_5_out_5), .Input(in_3), .Clr(Clear), .in_3(and_9_out));
  Register register_6 (.in_4(Clock), .out_5(register_6_out_5), .Input(in_3), .Clr(Clear), .in_3(and_11_out));
  Register register_7 (.in_4(Clock), .out_5(register_7_out_5), .Input(in_3), .Clr(Clear), .in_3(and_13_out));
  Register register_8 (.in_4(Clock), .out_5(register_8_out_5), .Input(in_3), .Clr(Clear), .in_3(and_15_out));
  Register register_9 (.in_4(Clock), .out_5(register_9_out_5), .Input(in_3), .Clr(Clear), .in_3(and_2_out));
  Register register_10 (.in_4(Clock), .out_5(register_10_out_5), .Input(in_3), .Clr(Clear), .in_3(and_4_out));
  Register register_11 (.in_4(Clock), .out_5(register_11_out_5), .Input(in_3), .Clr(Clear), .in_3(and_6_out));
  Register register_12 (.in_4(Clock), .out_5(register_12_out_5), .Input(in_3), .Clr(Clear), .in_3(and_8_out));
  Register register_13 (.in_4(Clock), .out_5(register_13_out_5), .Input(in_3), .Clr(Clear), .in_3(and_10_out));
  Register register_14 (.in_4(Clock), .out_5(register_14_out_5), .Input(in_3), .Clr(Clear), .in_3(and_12_out));
  Register register_15 (.in_4(Clock), .out_5(register_15_out_5), .Input(in_3), .Clr(Clear), .in_3(and_14_out));
  Register register_16 (.in_4(Clock), .out_5(register_16_out_5), .Input(in_3), .Clr(Clear), .in_3(and_16_out));
  Multiplexer #(.select(4), .width(18), .enable("false")) multiplexer_1 (
    .in0(register_1_out_5), .in1(register_9_out_5), .in2(register_2_out_5), .in3(register_10_out_5),
    .in4(register_3_out_5), .in5(register_11_out_5), .in6(register_4_out_5), .in7(register_12_out_5),
    .in8(register_5_out_5), .in9(register_13_out_5), .in10(register_6_out_5), .in11(register_14_out_5),
    .in12(register_7_out_5), .in13(register_15_out_5), .in14(register_8_out_5), .in15(register_16_out_5),
    .out(Output_1), .sel(Read_1_Bit));
  Multiplexer #(.select(4), .width(18), .enable("false")) multiplexer_2 (
    .in0(register_1_out_5), .in1(register_9_out_5), .in2(register_2_out_5), .in3(register_10_out_5),
    .in4(register_3_out_5), .in5(register_11_out_5), .in6(register_4_out_5), .in7(register_12_out_5),
    .in8(register_5_out_5), .in9(register_13_out_5), .in10(register_6_out_5), .in11(register_14_out_5),
    .in12(register_7_out_5), .in13(register_15_out_5), .in14(register_8_out_5), .in15(register_16_out_5),
    .out(Output), .sel(Read_2_Bit));
endmodule

module ALU (
  input  [17:0] INPUT1,
  input  [17:0] INPUT2,
  input  [1:0] ALU_Control_Input,
  output [17:0] out_4
);

  wire [17:0] and_1_out, n18_bit_adder_1_out_3, nor_1_out, not_1_out;

  _18_bit_adder u_18_bit_adder_1 (.in_1(INPUT1), .in_2(INPUT2), .out_3(n18_bit_adder_1_out_3));  // open: out_4
  assign and_1_out = INPUT1 & INPUT2;  // AND_Gate and_1, 18 bits wide
  assign nor_1_out = ~(INPUT1 | INPUT2);  // NOR_Gate nor_1, 18 bits wide
  assign not_1_out = ~and_1_out;  // NOT_Gate not_1, 18 bits wide
  Multiplexer #(.select(2), .width(18), .enable("false")) multiplexer_1 (
    .in0(n18_bit_adder_1_out_3), .in1(and_1_out), .in2(not_1_out), .in3(nor_1_out), .out(out_4),
    .sel(ALU_Control_Input));

  // Notes on the sheet:
  //   ADD - 00 // AND - 01 // NAND - 10 // NOR - 11 
endmodule

module Register (
  input  [17:0] Input,
  input  Clr,
  input  in_3,
  input  in_4,
  output [17:0] out_5
);

  wire or_1_out;
  wire [17:0] multiplexer_1_out, multiplexer_2_out;

  Multiplexer #(.width(18), .enable("false")) multiplexer_1 (
    .in0(Input), .in1({18{1'b0}}), .out(multiplexer_1_out), .sel(Clr));
  Multiplexer #(.width(18), .enable("false")) multiplexer_2 (
    .in0(out_5), .in1(multiplexer_1_out), .out(multiplexer_2_out), .sel(or_1_out));
  or or_1 (or_1_out, Clr, in_3);
  d_flipflop d_flipflop_1 (.D(multiplexer_2_out[0]), .C(in_4), .Q(out_5[0]));
  d_flipflop d_flipflop_2 (.D(multiplexer_2_out[1]), .C(in_4), .Q(out_5[1]));
  d_flipflop d_flipflop_3 (.D(multiplexer_2_out[2]), .C(in_4), .Q(out_5[2]));
  d_flipflop d_flipflop_4 (.D(multiplexer_2_out[3]), .C(in_4), .Q(out_5[3]));
  d_flipflop d_flipflop_5 (.D(multiplexer_2_out[4]), .C(in_4), .Q(out_5[4]));
  d_flipflop d_flipflop_6 (.D(multiplexer_2_out[5]), .C(in_4), .Q(out_5[5]));
  d_flipflop d_flipflop_7 (.D(multiplexer_2_out[6]), .C(in_4), .Q(out_5[6]));
  d_flipflop d_flipflop_8 (.D(multiplexer_2_out[7]), .C(in_4), .Q(out_5[7]));
  d_flipflop d_flipflop_9 (.D(multiplexer_2_out[8]), .C(in_4), .Q(out_5[8]));
  d_flipflop d_flipflop_10 (.D(multiplexer_2_out[9]), .C(in_4), .Q(out_5[9]));
  d_flipflop d_flipflop_11 (.D(multiplexer_2_out[10]), .C(in_4), .Q(out_5[10]));
  d_flipflop d_flipflop_12 (.D(multiplexer_2_out[11]), .C(in_4), .Q(out_5[11]));
  d_flipflop d_flipflop_13 (.D(multiplexer_2_out[12]), .C(in_4), .Q(out_5[12]));
  d_flipflop d_flipflop_14 (.D(multiplexer_2_out[13]), .C(in_4), .Q(out_5[13]));
  d_flipflop d_flipflop_15 (.D(multiplexer_2_out[14]), .C(in_4), .Q(out_5[14]));
  d_flipflop d_flipflop_16 (.D(multiplexer_2_out[15]), .C(in_4), .Q(out_5[15]));
  d_flipflop d_flipflop_17 (.D(multiplexer_2_out[16]), .C(in_4), .Q(out_5[16]));
  d_flipflop d_flipflop_18 (.D(multiplexer_2_out[17]), .C(in_4), .Q(out_5[17]));

  // Other names for the same wires on the sheet: Back[17:0] = out_5
endmodule

module d_latch (
  input  D,
  input  C,
  output Q
);

  wire and_1_out, and_2_out, nor_1_out, not_1_out;

  not not_1 (not_1_out, D);
  and and_1 (and_1_out, D, C);
  and and_2 (and_2_out, C, not_1_out);
  nor nor_1 (nor_1_out, and_1_out, Q);
  nor nor_2 (Q, nor_1_out, and_2_out);

  // Notes on the sheet:
  //   S1
  //   R1
  //   upperNOR
  //   lowerNOR
  //   Q2
  //   Q1
endmodule

module d_flipflop (
  input  D,
  input  C,
  output Q
);

  wire d_latch_1_q, not_1_out;

  d_latch d_latch_1 (.D(D), .C(C), .Q(d_latch_1_q));
  d_latch d_latch_2 (.D(d_latch_1_q), .C(not_1_out), .Q(Q));
  not not_1 (not_1_out, C);

  // Notes on the sheet:
  //   dl1
  //   Q1
  //   dl2
endmodule

module _1_bit_adder (
  input  A,
  input  B,
  input  Cin,
  output OUTPUT,
  output carryOut
);

  wire and_1_out, and_2_out, and_3_out;

  and and_1 (and_1_out, A, B);
  and and_2 (and_2_out, Cin, B);
  and and_3 (and_3_out, A, Cin);
  xor xor_1 (OUTPUT, A, B, Cin);
  or or_1 (carryOut, and_1_out, and_2_out, and_3_out);

  // Notes on the sheet:
  //   xorGate
  //   AandB
  //   Cin_and_B
  //   Cin_and_A
  //   orGate
endmodule

module _18_bit_adder (
  input  [17:0] in_1,
  input  [17:0] in_2,
  output [17:0] out_3,
  output out_4
);

  wire n1_bit_adder_1_carryout, n1_bit_adder_2_carryout, n1_bit_adder_3_carryout, n1_bit_adder_4_carryout,
       n1_bit_adder_5_carryout, n1_bit_adder_6_carryout, n1_bit_adder_7_carryout, n1_bit_adder_8_carryout,
       n1_bit_adder_9_carryout, n1_bit_adder_10_carryout, n1_bit_adder_11_carryout, n1_bit_adder_12_carryout,
       n1_bit_adder_13_carryout, n1_bit_adder_14_carryout, n1_bit_adder_15_carryout,
       n1_bit_adder_16_carryout, n1_bit_adder_17_carryout;

  _1_bit_adder u_1_bit_adder_1 (
    .A(in_1[0]), .B(in_2[0]), .Cin(1'b0), .OUTPUT(out_3[0]), .carryOut(n1_bit_adder_1_carryout));
  _1_bit_adder u_1_bit_adder_2 (
    .A(in_1[1]), .B(in_2[1]), .Cin(n1_bit_adder_1_carryout), .OUTPUT(out_3[1]),
    .carryOut(n1_bit_adder_2_carryout));
  _1_bit_adder u_1_bit_adder_3 (
    .A(in_1[2]), .B(in_2[2]), .Cin(n1_bit_adder_2_carryout), .OUTPUT(out_3[2]),
    .carryOut(n1_bit_adder_3_carryout));
  _1_bit_adder u_1_bit_adder_4 (
    .A(in_1[3]), .B(in_2[3]), .Cin(n1_bit_adder_3_carryout), .OUTPUT(out_3[3]),
    .carryOut(n1_bit_adder_4_carryout));
  _1_bit_adder u_1_bit_adder_5 (
    .A(in_1[4]), .B(in_2[4]), .Cin(n1_bit_adder_4_carryout), .OUTPUT(out_3[4]),
    .carryOut(n1_bit_adder_5_carryout));
  _1_bit_adder u_1_bit_adder_6 (
    .A(in_1[5]), .B(in_2[5]), .Cin(n1_bit_adder_5_carryout), .OUTPUT(out_3[5]),
    .carryOut(n1_bit_adder_6_carryout));
  _1_bit_adder u_1_bit_adder_7 (
    .A(in_1[6]), .B(in_2[6]), .Cin(n1_bit_adder_6_carryout), .OUTPUT(out_3[6]),
    .carryOut(n1_bit_adder_7_carryout));
  _1_bit_adder u_1_bit_adder_8 (
    .A(in_1[7]), .B(in_2[7]), .Cin(n1_bit_adder_7_carryout), .OUTPUT(out_3[7]),
    .carryOut(n1_bit_adder_8_carryout));
  _1_bit_adder u_1_bit_adder_9 (
    .A(in_1[8]), .B(in_2[8]), .Cin(n1_bit_adder_8_carryout), .OUTPUT(out_3[8]),
    .carryOut(n1_bit_adder_9_carryout));
  _1_bit_adder u_1_bit_adder_10 (
    .A(in_1[9]), .B(in_2[9]), .Cin(n1_bit_adder_9_carryout), .OUTPUT(out_3[9]),
    .carryOut(n1_bit_adder_10_carryout));
  _1_bit_adder u_1_bit_adder_11 (
    .A(in_1[10]), .B(in_2[10]), .Cin(n1_bit_adder_10_carryout), .OUTPUT(out_3[10]),
    .carryOut(n1_bit_adder_11_carryout));
  _1_bit_adder u_1_bit_adder_12 (
    .A(in_1[11]), .B(in_2[11]), .Cin(n1_bit_adder_11_carryout), .OUTPUT(out_3[11]),
    .carryOut(n1_bit_adder_12_carryout));
  _1_bit_adder u_1_bit_adder_13 (
    .A(in_1[12]), .B(in_2[12]), .Cin(n1_bit_adder_12_carryout), .OUTPUT(out_3[12]),
    .carryOut(n1_bit_adder_13_carryout));
  _1_bit_adder u_1_bit_adder_14 (
    .A(in_1[13]), .B(in_2[13]), .Cin(n1_bit_adder_13_carryout), .OUTPUT(out_3[13]),
    .carryOut(n1_bit_adder_14_carryout));
  _1_bit_adder u_1_bit_adder_15 (
    .A(in_1[14]), .B(in_2[14]), .Cin(n1_bit_adder_14_carryout), .OUTPUT(out_3[14]),
    .carryOut(n1_bit_adder_15_carryout));
  _1_bit_adder u_1_bit_adder_16 (
    .A(in_1[15]), .B(in_2[15]), .Cin(n1_bit_adder_15_carryout), .OUTPUT(out_3[15]),
    .carryOut(n1_bit_adder_16_carryout));
  _1_bit_adder u_1_bit_adder_17 (
    .A(in_1[16]), .B(in_2[16]), .Cin(n1_bit_adder_16_carryout), .OUTPUT(out_3[16]),
    .carryOut(n1_bit_adder_17_carryout));
  _1_bit_adder u_1_bit_adder_18 (
    .A(in_1[17]), .B(in_2[17]), .Cin(n1_bit_adder_17_carryout), .OUTPUT(out_3[17]), .carryOut(out_4));
endmodule

module _6_18extender (
  input  [5:0] \input ,
  output [17:0] \output 
);


  assign \output  = {{13{\input [5]}}, \input [4:0]};
endmodule

module _14_18extender (
  input  [13:0] \input ,
  output [17:0] out_2
);


  assign out_2 = {{5{\input [13]}}, \input [12:0]};
endmodule

module _18_bit_comperator (
  input  [17:0] in_1,
  input  [17:0] in_2,
  output out_3,
  output out_4,
  output out_5
);

  wire not_1_out, not_2_out;
  wire [16:0] n18_bit_adder_1_out_3;
  wire [17:0] n18_bit_revers_1_out_2;

  _18_bit_revers u_18_bit_revers_1 (.in_1(in_1), .out_2(n18_bit_revers_1_out_2));
  _18_bit_adder u_18_bit_adder_1 (
    .in_1(n18_bit_revers_1_out_2), .in_2(in_2), .out_3({out_3, n18_bit_adder_1_out_3}));  // open: out_4
  not not_1 (not_1_out, out_3);
  not not_2 (not_2_out, out_4);
  and and_1 (out_5, not_1_out, not_2_out);
  // Probe on {out_3, n18_bit_adder_1_out_3}
  nor nor_1 (out_4, out_3, n18_bit_adder_1_out_3[16], n18_bit_adder_1_out_3[15], n18_bit_adder_1_out_3[14], n18_bit_adder_1_out_3[13], n18_bit_adder_1_out_3[12], n18_bit_adder_1_out_3[11], n18_bit_adder_1_out_3[10], n18_bit_adder_1_out_3[9], n18_bit_adder_1_out_3[8], n18_bit_adder_1_out_3[7], n18_bit_adder_1_out_3[6], n18_bit_adder_1_out_3[5], n18_bit_adder_1_out_3[4], n18_bit_adder_1_out_3[3], n18_bit_adder_1_out_3[2], n18_bit_adder_1_out_3[1], n18_bit_adder_1_out_3[0]);
endmodule

// Reverser
module _18_bit_revers (
  input  [17:0] in_1,
  output [17:0] out_2
);

  wire [17:0] not_1_out;

  assign not_1_out = ~in_1;  // NOT_Gate not_1, 18 bits wide
  _18_bit_adder u_18_bit_adder_1 (.in_1(18'h1), .in_2(not_1_out), .out_3(out_2));  // open: out_4
endmodule
